// Logisim project Guia_0503.circ as structural Verilog: 1 circuit, main circuit main
module main (
  input  a,
  input  b,
  output s
);

  // NOR_Gate nor_1 has open pins: out=a
  // NOR_Gate nor_2 has open pins: out=b

  assign s = b;
endmodule
