// Logisim project Guia_0506.circ as structural Verilog: 1 circuit, main circuit main
module main (
  input  a,
  input  b,
  output s
);

  // NAND_Gate nand_1 has open pins: out=a
  // NAND_Gate nand_2 has open pins: out=b

  assign s = b;
endmodule
