// Logisim project Guia_0701.circ as structural Verilog: 1 circuit, main circuit main
module main (
  input  x,
  input  y,
  input  s,
  output z
);

  wire AND_out, NAND_out;

  and AND (AND_out, x, y);
  nand NAND (NAND_out, x, y);
  // MUX_2x1 mux_2x1_1: pin names not known; wires that end beside it: x, y, AND_out, NAND_out, s, z

  // Notes on the sheet:
  //   Guia_0701
  //   Daniel Matos Marques - 800712
endmodule
