// Logisim project Guia_0702.circ as structural Verilog: 1 circuit, main circuit main
module main (
  input  x,
  input  y,
  input  s,
  output z
);

  wire NOR_out, OR_out;

  or OR (OR_out, x, y);
  nor NOR (NOR_out, x, y);
  // MUX_2x1 mux_2x1_1: pin names not known; wires that end beside it: x, y, OR_out, NOR_out, s, z

  // Notes on the sheet:
  //   Guia_0702
  //   Daniel Matos Marques - 800712
endmodule
