// Logisim project Guia_0704.circ as structural Verilog: 1 circuit, main circuit main
module main (
  input  x,
  input  y,
  input  in_3,
  input  in_4,
  output z
);

  wire NOR_out, OR_out, XNOR_out, XOR_out;

  or OR (OR_out, x, y);
  nor NOR (NOR_out, x, y);
  xor XOR (XOR_out, x, y);
  xnor XNOR (XNOR_out, x, y);
  // MUX_4x2 mux_4x2_1: pin names not known; wires that end beside it: OR_out, NOR_out, XOR_out, XNOR_out, in_3, in_4, z

  // Notes on the sheet:
  //   Guia_0704
  //   Daniel Matos Marques - 800712
endmodule
