// Logisim project exercicio03_mux.circ as structural Verilog: 1 circuit
module main (
);

  wire multiplexer_1_p4, multiplexer_2_p4, multiplexer_3_p4, not_1_p1, not_1_p2, not_2_p1, not_2_p2,
       not_3_p1, not_3_p2;

  // Pin a: pin names not known
  // Pin b: pin names not known
  // Pin c: pin names not known
  // NOT_Gate not_1: pin names not known; wires that end beside it: not_1_p1, not_1_p2
  // NOT_Gate not_2: pin names not known; wires that end beside it: not_2_p1, not_2_p2
  // NOT_Gate not_3: pin names not known; wires that end beside it: not_3_p1, not_3_p2
  // Multiplexer multiplexer_1: pin names not known; wires that end beside it: not_1_p1, not_1_p2, not_2_p1, multiplexer_1_p4
  // Multiplexer multiplexer_2: pin names not known; wires that end beside it: not_2_p2, not_3_p1, not_3_p1, multiplexer_2_p4
  // Multiplexer multiplexer_3: pin names not known; wires that end beside it: multiplexer_1_p4, multiplexer_2_p4, not_3_p2, multiplexer_3_p4
  // Pin s: pin names not known; wires that end beside it: multiplexer_3_p4
endmodule
