// Logisim project Q4.circ as structural Verilog
module Da (
  input  a,
  input  b,
  input  c,
  output out_4
);

  wire and_1_out, and_2_out, not_1_out, not_2_out, not_3_out;

  not not_1 (not_1_out, a);
  not not_2 (not_2_out, b);
  not not_3 (not_3_out, c);
  and and_1 (and_1_out, b, c);
  and and_2 (and_2_out, a, not_3_out);
  or or_1 (out_4, and_1_out, and_2_out);

  // Notes on the sheet:
  //   Da
endmodule

module JaKa (
  input  a,
  input  b,
  input  c,
  input  a_2,
  input  b_2,
  input  c_2,
  output out_7,
  output out_8
);

  wire and_1_out, and_2_out, and_3_out, and_4_out, not_1_out, not_2_out, not_3_out, not_4_out, not_5_out,
       not_6_out;

  not not_1 (not_1_out, a);
  not not_2 (not_2_out, a_2);
  not not_3 (not_3_out, b);
  not not_4 (not_4_out, c);
  not not_5 (not_5_out, c_2);
  not not_6 (not_6_out, b_2);
  and and_1 (and_1_out, b, c);
  and and_2 (and_2_out, a, not_4_out);
  and and_3 (and_3_out, not_2_out, not_5_out);
  and and_4 (and_4_out, not_6_out, c_2);
  or or_1 (out_7, and_1_out, and_2_out);
  or or_2 (out_8, and_3_out, and_4_out);

  // Notes on the sheet:
  //   Sa
  //   Ra
endmodule

module Ta (
  input  a,
  input  b,
  input  c,
  output out_4
);

  wire and_1_out, and_2_out, not_1_out, not_2_out, not_3_out;

  not not_1 (not_1_out, a);
  not not_2 (not_2_out, c);
  not not_3 (not_3_out, b);
  and and_1 (and_1_out, not_1_out, b, c);
  and and_2 (and_2_out, a, not_3_out, c);
  or or_1 (out_4, and_1_out, and_2_out);

  // Notes on the sheet:
  //   Ta
endmodule

module SbRb (
  input  a,
  input  b,
  input  c,
  input  a_2,
  input  b_2,
  input  c_2,
  output out_7,
  output out_8
);

  wire not_1_out, not_2_out, not_3_out, not_4_out, not_5_out, not_6_out;

  not not_1 (not_1_out, a);
  not not_2 (not_2_out, a_2);
  not not_3 (not_3_out, c);
  not not_4 (not_4_out, b);
  not not_5 (not_5_out, b_2);
  not not_6 (not_6_out, c_2);
  buf and_1 (out_7, b);  // AND_Gate
  buf and_2 (out_8, not_5_out);  // AND_Gate

  // Notes on the sheet:
  //   Sb
  //   Rb
endmodule

module Tb (
  input  a,
  input  b,
  input  c,
  output out_4
);

  wire and_1_out, and_2_out, not_1_out, not_2_out, not_3_out;

  not not_1 (not_1_out, a);
  not not_2 (not_2_out, b);
  not not_3 (not_3_out, c);
  and and_1 (and_1_out, not_1_out, not_2_out, c);
  and and_2 (and_2_out, a, b, c);
  or or_1 (out_4, and_1_out, and_2_out);

  // Notes on the sheet:
  //   Tb
  //   a'b'c + abc
endmodule
