// Logisim project Q5.circ as structural Verilog
module SR_RIGHT_LOAD (
  input  [3:0] in_1,
  input  LOAD,
  input  CLEAR
);

  wire and_1_out, and_2_out, and_3_out, and_4_out, CLK_out, d_ff_1_q, d_ff_2_q, d_ff_3_q, d_ff_4_q,
       xor_1_out, xor_2_out, xor_3_out, xor_4_out;

  Clock CLK (.out(CLK_out));
  and and_1 (and_1_out, in_1[3], LOAD);
  xor xor_1 (xor_1_out, d_ff_4_q, and_1_out);
  and and_2 (and_2_out, in_1[2], LOAD);
  D_Flip_Flop d_ff_1 (.clk(CLK_out), .D(xor_1_out), .Q(d_ff_1_q), .reset(CLEAR));  // open: Qn, preset
  xor xor_2 (xor_2_out, d_ff_1_q, and_2_out);
  D_Flip_Flop d_ff_2 (.clk(CLK_out), .D(xor_2_out), .Q(d_ff_2_q), .reset(CLEAR));  // open: Qn, preset
  and and_3 (and_3_out, in_1[1], LOAD);
  xor xor_3 (xor_3_out, d_ff_2_q, and_3_out);
  and and_4 (and_4_out, in_1[0], LOAD);
  D_Flip_Flop d_ff_3 (.clk(CLK_out), .D(xor_3_out), .Q(d_ff_3_q), .reset(CLEAR));  // open: Qn, preset
  xor xor_4 (xor_4_out, d_ff_3_q, and_4_out);
  D_Flip_Flop d_ff_4 (.clk(CLK_out), .D(xor_4_out), .Q(d_ff_4_q), .reset(CLEAR));  // open: Qn, preset

  // Notes on the sheet:
  //   Registrador de Deslocamento para a Direita com Load
endmodule

module SR_LEFT_LOAD (
  input  [3:0] in_1,
  input  LOAD,
  input  CLEAR
);

  wire and_1_out, and_2_out, and_3_out, and_4_out, CLK_out, d_ff_1_q, d_ff_2_q, d_ff_3_q, d_ff_4_q,
       xor_1_out, xor_2_out, xor_3_out, xor_4_out;

  Clock CLK (.out(CLK_out));
  and and_1 (and_1_out, in_1[3], LOAD);
  xor xor_1 (xor_1_out, d_ff_2_q, and_1_out);
  and and_2 (and_2_out, in_1[2], LOAD);
  D_Flip_Flop d_ff_1 (.clk(CLK_out), .D(xor_1_out), .Q(d_ff_1_q), .reset(CLEAR));  // open: Qn, preset
  xor xor_2 (xor_2_out, d_ff_3_q, and_2_out);
  D_Flip_Flop d_ff_2 (.clk(CLK_out), .D(xor_2_out), .Q(d_ff_2_q), .reset(CLEAR));  // open: Qn, preset
  and and_3 (and_3_out, in_1[1], LOAD);
  xor xor_3 (xor_3_out, d_ff_4_q, and_3_out);
  and and_4 (and_4_out, in_1[0], LOAD);
  D_Flip_Flop d_ff_3 (.clk(CLK_out), .D(xor_3_out), .Q(d_ff_3_q), .reset(CLEAR));  // open: Qn, preset
  xor xor_4 (xor_4_out, d_ff_1_q, and_4_out);
  D_Flip_Flop d_ff_4 (.clk(CLK_out), .D(xor_4_out), .Q(d_ff_4_q), .reset(CLEAR));  // open: Qn, preset

  // Notes on the sheet:
  //   Registrador de Deslocamento para a Esquerda com Load
endmodule

module SR_RIGHT_LOAD_XOR (
  input  [3:0] in_1,
  input  LOAD,
  input  \input ,
  input  CLEAR
);

  wire and_1_out, and_2_out, and_3_out, and_4_out, CLK_out, d_ff_1_q, d_ff_2_q, d_ff_3_q, d_ff_4_q,
       xor_1_out, xor_2_out, xor_3_out, xor_4_out, xor_5_out;

  Clock CLK (.out(CLK_out));
  and and_1 (and_1_out, in_1[3], LOAD);
  xor xor_1 (xor_1_out, d_ff_4_q, and_1_out);
  xor xor_2 (xor_2_out, xor_1_out, \input );
  and and_2 (and_2_out, in_1[2], LOAD);
  D_Flip_Flop d_ff_1 (.clk(CLK_out), .D(xor_2_out), .Q(d_ff_1_q), .reset(CLEAR));  // open: Qn, preset
  xor xor_3 (xor_3_out, d_ff_1_q, and_2_out);
  D_Flip_Flop d_ff_2 (.clk(CLK_out), .D(xor_3_out), .Q(d_ff_2_q), .reset(CLEAR));  // open: Qn, preset
  and and_3 (and_3_out, in_1[1], LOAD);
  xor xor_4 (xor_4_out, d_ff_2_q, and_3_out);
  and and_4 (and_4_out, in_1[0], LOAD);
  D_Flip_Flop d_ff_3 (.clk(CLK_out), .D(xor_4_out), .Q(d_ff_3_q), .reset(CLEAR));  // open: Qn, preset
  xor xor_5 (xor_5_out, d_ff_3_q, and_4_out);
  D_Flip_Flop d_ff_4 (.clk(CLK_out), .D(xor_5_out), .Q(d_ff_4_q), .reset(CLEAR));  // open: Qn, preset

  // Notes on the sheet:
  //   Registrador de Deslocamento para a Direita com Load com entrada XOR
endmodule

module SR_LEFT_LOAD_NAND (
  input  [3:0] in_1,
  input  LOAD,
  input  \input ,
  input  CLEAR
);

  wire and_1_out, and_2_out, and_3_out, and_4_out, CLK_out, d_ff_1_q, d_ff_2_q, d_ff_3_q, d_ff_4_q,
       nand_1_out, xor_1_out, xor_2_out, xor_3_out, xor_4_out;

  Clock CLK (.out(CLK_out));
  nand nand_1 (nand_1_out, xor_1_out, \input );
  and and_1 (and_1_out, in_1[3], LOAD);
  xor xor_1 (xor_1_out, d_ff_2_q, and_1_out);
  and and_2 (and_2_out, in_1[2], LOAD);
  D_Flip_Flop d_ff_1 (.clk(CLK_out), .D(nand_1_out), .Q(d_ff_1_q), .reset(CLEAR));  // open: Qn, preset
  xor xor_2 (xor_2_out, d_ff_3_q, and_2_out);
  D_Flip_Flop d_ff_2 (.clk(CLK_out), .D(xor_2_out), .Q(d_ff_2_q), .reset(CLEAR));  // open: Qn, preset
  and and_3 (and_3_out, in_1[1], LOAD);
  xor xor_3 (xor_3_out, d_ff_4_q, and_3_out);
  and and_4 (and_4_out, in_1[0], LOAD);
  D_Flip_Flop d_ff_3 (.clk(CLK_out), .D(xor_3_out), .Q(d_ff_3_q), .reset(CLEAR));  // open: Qn, preset
  xor xor_4 (xor_4_out, d_ff_1_q, and_4_out);
  D_Flip_Flop d_ff_4 (.clk(CLK_out), .D(xor_4_out), .Q(d_ff_4_q), .reset(CLEAR));  // open: Qn, preset

  // Notes on the sheet:
  //   Registrador de Deslocamento para a Esquerda com Load com entrada NAND
endmodule

module SR_RIGHT__QtoD (
  input  [3:0] in_1,
  input  LOAD,
  input  CLEAR
);

  wire and_1_out, and_2_out, and_3_out, and_4_out, CLK_out, d_ff_1_qn, d_ff_2_qn, d_ff_3_qn, d_ff_4_qn,
       xor_1_out, xor_2_out, xor_3_out, xor_4_out;

  Clock CLK (.out(CLK_out));
  and and_1 (and_1_out, in_1[3], LOAD);
  xor xor_1 (xor_1_out, d_ff_4_qn, and_1_out);
  and and_2 (and_2_out, in_1[2], LOAD);
  D_Flip_Flop d_ff_1 (.clk(CLK_out), .D(xor_1_out), .Qn(d_ff_1_qn), .reset(CLEAR));  // open: Q, preset
  xor xor_2 (xor_2_out, d_ff_1_qn, and_2_out);
  D_Flip_Flop d_ff_2 (.clk(CLK_out), .D(xor_2_out), .Qn(d_ff_2_qn), .reset(CLEAR));  // open: Q, preset
  and and_3 (and_3_out, in_1[1], LOAD);
  xor xor_3 (xor_3_out, d_ff_2_qn, and_3_out);
  and and_4 (and_4_out, in_1[0], LOAD);
  D_Flip_Flop d_ff_3 (.clk(CLK_out), .D(xor_3_out), .Qn(d_ff_3_qn), .reset(CLEAR));  // open: Q, preset
  xor xor_4 (xor_4_out, d_ff_3_qn, and_4_out);
  D_Flip_Flop d_ff_4 (.clk(CLK_out), .D(xor_4_out), .Qn(d_ff_4_qn), .reset(CLEAR));  // open: Q, preset

  // Notes on the sheet:
  //   Registrador de Deslocamento para a Direita com Load
endmodule
